# Fritzing sketch CONNECTIONS (saved by Fritzing 1.0.5)
breadboards: 2

parts:
  Part1 = Solar Panel [package="Renogy 50 Watts 12 Volt Monocrystalline Bendable Solar Panel"]
  Part2 = Solar Charge Controller [part_number="HGX Series Solar Charge Controller PWM" package=PWM-Model]
  BAT1 = 12 battery [package=battery]
  Mod1 = Raspberry Pi 4B  # not connected
  Mod2 = Amica NodeMCU DEVKIT 1.0
  A1 = 2 channel relay module [package=THT]
  M1 = RioRand LM2596
  A2 = 2 channel relay module [package=THT]
  Mod3 = Amica NodeMCU DEVKIT 1.0
  M2 = 1 chan 5v relay module
  Disp1 = 38mm 8x8 dot matrix row cathode led display with narrow pcb pads
  S2 = Pushbutton [package="[SMD]"]
  LED1 = smd LED [color="Red (633nm)" package="1206 [SMD]"]
  LED2 = smd LED [color="Red (633nm)" package="1206 [SMD]"]
  LED3 = smd LED [color="Red (633nm)" package="1206 [SMD]"]
  INA1 = INA219 DC Current Sensor Breakout

nets:
  N1: Part1.Connector_1, Part2.Connector_1
  N2: Part1.Connector_2, Part2.Connector_2
  N3: Part2.Connector_3, BAT1.+
  N4: Part2.Connector_4, BAT1.-
  N5: Part2.Connector_5, M1.Pin_1
  N6: Part2.Connector_6, M1.Pin_2
  N7: Mod2.pin1, Mod2.pin_10, Mod2.pin_26
  N8: Mod2.pin2, Mod2.pin_9, Mod2.pin_25, Mod2.pin_29, A1.Pin_26, M1.Pin_4, A2.Pin_26, Mod3.pin2, Mod3.pin_9, Mod3.pin_25, Mod3.pin_29, M2.pin_2
  N9: Mod2.pin_30, A1.Pin_25, M1.Pin_3, A2.Pin_25, Mod3.pin_30, M2.pin_1, INA1.Vin+2
  N10: A1.Pin_4, LED3.anode
  N11: A1.Pin_5, A1.Pin_8, A1.Pin_11, INA1.Vin-2
  N12: A1.Pin_7, LED2.anode
  N13: A1.Pin_10, S2.Pin_3, S2.Pin_4, LED1.anode
  N14: Mod3.pin1, Mod3.pin_10, Mod3.pin_26
  N15: Disp1.pin_3, S2.Pin_1, S2.Pin_2

custom parts:
  Solar Panel: Renogy 50 Watts 12 Volt Solar Panel
  Solar Charge Controller: PWM-Solar Charge Controller
  12 battery: 12V lead acid type battery, like the Husqvarna YTH2448 12V 35AH battery. This is the mini version 1/4 the size of the actual battery to be closer to typical breadboard parts (around 2in wide rathher than 7in). The pads in pcb are sized to accomidate up to 14ga wire (as these batterys will deliver high currents.)
  2 channel relay module: 4 channel Relay Module 5V 12V 24V High and Low Level Trigger Relay Control With Optocoupler Two Way relays DC 5 V 12 V 24 V Volt.
  1 chan 5v relay module: 1 Channel 5V Relay Module Board Shield with Optocoupler Support High and Low Level Trigger for Arduino.
  INA219 DC Current Sensor Breakout: INA DC Current Sensor Breakout
